# Fritzing sketch togglemic (saved by Fritzing 0.9.6b)
breadboards: 1

parts:
  LED1 = LED - 3mm [color="Red (633nm)" package="3 mm [THT]"]
  S1 = Round Pushbutton
  part = Resistor [tolerance=±5% resistance=1k package="2512 [SMD]"]
  Bauteil1 = Arduino Micro (Rev3)
  R2 = Resistor [tolerance=±5% resistance=10k package="2512 [SMD]"]

nets:
  N1: LED1.cathode, Bauteil1.GND, R2.Pin_1
  N2: LED1.anode, part.Pin_0
  N3: S1.leg0, Bauteil1.D5_PWM, R2.Pin_0
  N4: S1.leg1, Bauteil1.5V
  N5: part.Pin_1, Bauteil1.D7
